# Fritzing sketch ConnectionSchematic (saved by Fritzing 0.9.3b)
breadboards: 1

parts:
  Raspberry_Pi_1 = Raspberry Pi 3 [part_number=RPI-3-V1.2]
  HC-SR04_Sensor_1 = HC-SR04 Ultrasonic Distance Sensor
  R1 = Resistor [tolerance=±5% resistance=1k package=THT]
  R2 = Resistor [tolerance=±5% resistance=1k package="2010 [SMD]"]
  R3 = Resistor [tolerance=±5% resistance=1k package="2010 [SMD]"]
  LED1 = LED - 5mm [color="Red (633nm)" package="5 mm [THT]"]
  LED2 = LED - 5mm [color="Red (633nm)" package="5 mm [THT]"]
  R4 = Resistor [tolerance=±5% resistance=220 package=THT]
  R5 = Resistor [tolerance=±5% resistance=220 package=THT]

nets:
  N1: Raspberry_Pi_1.GPIO24, R1.Pin_1, R2.Pin_0
  N2: Raspberry_Pi_1.GPIO18, HC-SR04_Sensor_1.TRIG
  N3: Raspberry_Pi_1.GPIO15, R5.Pin_1
  N4: Raspberry_Pi_1.GPIO14, R4.Pin_1
  GND: Raspberry_Pi_1.GND, HC-SR04_Sensor_1.GND, R3.Pin_1, LED1.cathode, LED2.cathode
  5V: Raspberry_Pi_1.5V, HC-SR04_Sensor_1.VCC
  N5: HC-SR04_Sensor_1.ECHO, R1.Pin_0
  N6: R2.Pin_1, R3.Pin_0
  N7: LED1.anode, R4.Pin_0
  N8: LED2.anode, R5.Pin_0
